# Fritzing sketch Practica 4 proto (saved by Fritzing 0.9.3b)
breadboards: 1

parts:
  R1 = Resistor [tolerance=±5% resistance=47k package=THT]
  U1 = LM124-324 Quad Opamp [package="DIP (Dual Inline)"]
  U2 = POT [package=pot_mammoth]
  R5 = Resistor [tolerance=±5% resistance=1k package=THT]
  D1 = Diode [package=diode-1n4148]
  R6 = Resistor [tolerance=±5% resistance=1k package=THT]
  R7 = Resistor [tolerance=±5% resistance=15k package=THT]
  R8 = Resistor [tolerance=±5% resistance=15k package=THT]
  R9 = Resistor [tolerance=±5% resistance=10k package=THT]
  R10 = Resistor [tolerance=±5% resistance=10k package=THT]

nets:
  N1: R1.Pin_0, U2.S
  N2: R1.Pin_1, R5.Pin_1
  N3: U1.1OUT, R10.Pin_0
  N4: U1.1IN-, R6.Pin_1, R8.Pin_1
  N5: U1.1IN+, U2.A
  N6: U1.VCC-, U2.E
  N7: R5.Pin_0, D1.C, R6.Pin_0
  N8: R7.Pin_0, R9.Pin_1
  N9: R7.Pin_1, R8.Pin_0
  N10: R9.Pin_0, R10.Pin_1
